# Fritzing sketch AtariPaddles4 (saved by Fritzing 0.9.6b)
circuit board: 8.46667cm x 5.64444cm
breadboards: 2

parts:
  Part2 = Arduino Micro (Rev3)
  S1 = Round Pushbutton
  S2 = Round Pushbutton
  R1 = Rotary Potentiometer (Large) [maximum_resistance=100kΩ knob_status=50% package=THT]
  R2 = Rotary Potentiometer (Large) [maximum_resistance=100kΩ knob_status=50% package=THT]
  LED1 = LED - 5mm [color="Red (633nm)" current=0.030 package="5 mm [THT]"]
  LED2 = LED - 5mm [color="Red (633nm)" current=0.030 package="5 mm [THT]"]
  LED3 = LED - 5mm [color="Red (633nm)" current=0.030 package="5 mm [THT]"]
  LED4 = LED - 5mm [color="Red (633nm)" current=0.030 package="5 mm [THT]"]
  R3 = Resistor [tolerance=±5% resistance=220 package="2010 [SMD]"]
  R5 = Resistor [tolerance=±5% resistance=220 package="2010 [SMD]"]
  R6 = Resistor [tolerance=±5% resistance=220 package="2010 [SMD]"]
  J1 = Dagu DGServo 9g header (male) [package=THT]
  J2 = Dagu DGServo 9g header (male) [package=THT]
  R4 = Resistor [tolerance=±5% resistance=220 package="2010 [SMD]"]
  R7 = Resistor [tolerance=±5% resistance=220 package="2010 [SMD]"]
  R8 = Resistor [tolerance=±5% resistance=220 package="2010 [SMD]"]
  R10 = Resistor [tolerance=±5% resistance=470 package="2010 [SMD]"]
  R9 = Resistor [tolerance=±5% resistance=470 power=0.25 package=THT]
  J3 = Dagu DGServo 9g header (male) [package=THT]
  J4 = Dagu DGServo 9g header (male) [package=THT]
  J5 = Dagu DGServo 9g header (male) [package=THT]
  S4 = Pushbutton [package="[THT]"]
  S5 = Pushbutton [package="[THT]"]
  S6 = Pushbutton [package="[THT]"]
  S7 = Pushbutton [package="[THT]"]
  S8 = Pushbutton [package="[THT]"]
  R11 = Resistor [tolerance=±5% resistance=220 package="2010 [SMD]"]
  R12 = Resistor [tolerance=±5% resistance=220 package="2010 [SMD]"]
  R13 = Resistor [tolerance=±5% resistance=220 package="2010 [SMD]"]
  R14 = Resistor [tolerance=±5% resistance=220 package="2010 [SMD]"]
  R15 = Resistor [tolerance=±5% resistance=220 package="2010 [SMD]"]

nets (from the breadboard view):
  N1: Part2.D2/SDA, LED4.anode
  N2: Part2.D3/SCL, LED1.anode
  N3: Part2.D4_PWM/A6, LED2.anode
  N4: Part2.D5_PWM, LED3.anode
  5V: Part2.5V, J2.Vcc, J2.pulse
  N5: S1.leg0, J4.gnd
  N6: S1.leg1, S2.leg1, J4.Vcc
  N7: S2.leg0, J5.pulse
  N8: R1.leg1, R2.leg1, J3.gnd
  N9: R1.wiper, J4.pulse
  N10: R2.wiper, J3.Vcc
  N11: LED1.cathode, R4.Pin_0
  N12: LED2.cathode, R6.Pin_0
  N13: LED3.cathode, R3.Pin_0
  N14: LED4.cathode, R5.Pin_0
  N15: R3.Pin_1, R5.Pin_1, R6.Pin_1, J1.Vcc, R4.Pin_1, R7.Pin_0, R8.Pin_0, R8.Pin_1, R10.Pin_1, R9.Pin_1, S4.Pin_1, S4.Pin_2, S5.Pin_1, S5.Pin_2, S6.Pin_1, S6.Pin_2, S7.Pin_1, S7.Pin_2, S8.Pin_1, S8.Pin_2, R11.Pin_0, R11.Pin_1, R12.Pin_0, R12.Pin_1, R13.Pin_0, R13.Pin_1, R14.Pin_0, R14.Pin_1, R15.Pin_0, R15.Pin_1
  N16: J1.gnd, R10.Pin_0
  N17: J1.pulse, R7.Pin_1
  N18: J2.gnd, R9.Pin_0
  N19: S4.Pin_3, S4.Pin_4
  N20: S5.Pin_3, S5.Pin_4
  N21: S6.Pin_3, S6.Pin_4
  N22: S7.Pin_3, S7.Pin_4
  N23: S8.Pin_3, S8.Pin_4

notes:
  3-Button right
  4-Button Left
  5-Analog Left
  7-GND pin 5,9
  8-GND pin 3,4
  9-AnalogRight
  D5432
  BACK VIEW
  5 4 3 2 1
  9 8 7 6
  987 543
  A01-Paddle
  LED
  Pin=2345
  34 Button 8GND
  59 Wiper 7GND
  123
  456
  789
  123 456 789
  XX3 45 x789
